// Logisim project Brandon-ALU-Project.circ as structural Verilog: 2 circuits, main circuit 4 Bit ALU
module _1_bit_ALU (
  input  A,
  input  B,
  input  Cin,
  input  [1:0] Op,
  output Function_Output,
  output Cout
);

  wire adder_1_out, and_1_out, not_1_out, or_1_out;

  and and_1 (and_1_out, A, B);
  or or_1 (or_1_out, A, B);
  not not_1 (not_1_out, B);
  Adder #(.width(1)) adder_1 (.a(A), .b(B), .out(adder_1_out), .cin(Cin), .cout(Cout));
  Multiplexer #(.select(2), .enable("false")) multiplexer_1 (
    .in0(and_1_out), .in1(or_1_out), .in2(not_1_out), .in3(adder_1_out), .out(Function_Output), .sel(Op));
endmodule

module _4_Bit_ALU (
  input  [1:0] OPCODE,
  input  [3:0] B,
  input  [3:0] A,
  output [3:0] Output_Register,
  output [3:0] STATUS_Register
);

  _1_bit_ALU u_1_bit_alu_1 (
    .Function_Output(Output_Register[0]), .A(A[0]), .B(B[0]), .Op(OPCODE), .Cout(STATUS_Register[0]));  // open: Cin
  _1_bit_ALU u_1_bit_alu_2 (
    .Function_Output(Output_Register[1]), .A(A[1]), .B(B[1]), .Op(OPCODE), .Cout(STATUS_Register[1]));  // open: Cin
  _1_bit_ALU u_1_bit_alu_3 (
    .Function_Output(Output_Register[2]), .A(A[2]), .B(B[2]), .Op(OPCODE), .Cout(STATUS_Register[2]));  // open: Cin
  _1_bit_ALU u_1_bit_alu_4 (
    .Function_Output(Output_Register[3]), .A(A[3]), .B(B[3]), .Op(OPCODE), .Cout(STATUS_Register[3]));  // open: Cin

  // Notes on the sheet:
  //   STATUS_Register: pull=down
endmodule
